# Fritzing sketch schaltplan (saved by Fritzing 1.0.4)
breadboards: 2

parts:
  M1 = gear-motor
  M2 = gear-motor
  U1 = ESP32-38PinWide [part_number=ESP32-38PinWide]
  S3 = H-Bridge with L298N
  VCC1 = Battery block 9V [internal_resistance=0.1Ω]
  J1 = Piezo Speaker
  LED1 = LED - 5mm [color="Red (633nm)" current=0.030A package="5 mm [THT]"]
  LED2 = LED - 5mm [color="Red (633nm)" current=0.030A package="5 mm [THT]"]
  LED3 = LED - 5mm [color="Red (633nm)" current=0.030A package="5 mm [THT]"]
  R2 = Resistor [tolerance=±5% resistance=100 package="0805 [SMD]"]
  R3 = Resistor [tolerance=±5% resistance=100 package="0805 [SMD]"]
  R4 = Resistor [tolerance=±5% resistance=100 package="0805 [SMD]"]
  R5 = Resistor [tolerance=±5% resistance=300 package="0805 [SMD]"]
  S4 = Pushbutton [package="[SMD]"]
  S5 = Pushbutton [package="[SMD]"]

nets:
  N1: M1.pin_1, S3.M1-02
  N2: M1.pin_2, S3.M1-01
  N3: M2.pin_1, S3.M2-02
  N4: M2.pin_2, S3.M2-01
  N5: U1.connector0, S4.Pin_3, S4.Pin_4, S5.Pin_3, S5.Pin_4
  N6: U1.connector7, S3.ENB
  N7: U1.connector8, S3.IN4
  N8: U1.connector9, S3.IN3
  N9: U1.connector10, S3.ENA
  N10: U1.connector11, S3.IN2
  N11: U1.connector12, S3.IN1
  N12: U1.connector17, S3.GND, VCC1.-, R5.Pin_0
  N13: U1.connector18, S3.12V, VCC1.+
  N14: U1.connector28, R5.Pin_1, S4.Pin_1, S4.Pin_2, S5.Pin_1, S5.Pin_2
  N15: U1.connector30, R3.Pin_1
  N16: U1.connector32, R4.Pin_1
  N17: U1.connector37, J1.pin1, LED1.cathode, LED2.cathode, LED3.cathode
  N18: LED1.anode, R4.Pin_0
  N19: LED2.anode, R3.Pin_0
  N20: LED3.anode, R2.Pin_0

custom parts:
  H-Bridge with L298N: h-bridge
